// Logisim project groups.circ as structural Verilog: 3 circuits, main circuit groups
module test_group (
  output [31:0] out_1
);

  wire Clk_out, groups_1_rdy, tester_1_clk_out, tester_1_fail, tester_1_start, tester_1_success;
  wire [31:0] tester_1_x;

  // Probe on tester_1_x
  Clock Clk (.out(Clk_out));
  LED led_1 (.in(tester_1_fail));
  groups groups_1 (.x(tester_1_x), .start(tester_1_start), .clk(tester_1_clk_out), .z(out_1), .rdy(groups_1_rdy));
  tester tester_1 (
    .clk_in(Clk_out), .z(out_1), .rdy(groups_1_rdy), .x(tester_1_x), .start(tester_1_start),
    .clk_out(tester_1_clk_out), .fail(tester_1_fail), .success(tester_1_success));
  LED led_2 (.in(tester_1_success));
  // Probe on out_1
  // Probe on groups_1_rdy

  // Notes on the sheet:
  //   Red means failure:
  //   the outputs z or rdy
  //   wrong for the input x.
  //   You need to debug your circuit.
  //   the full timing diagram
  //   Congratulations!
  //   Green means success
  //   Your solution matches
  //   To debug your circuit
  //   with the hand from here,
  //   not from the left panel.
  //   enter to the module GROUPS
endmodule

module groups (
  input  [31:0] x,
  input  start,
  input  clk,
  output rdy,
  output [31:0] z
);

  wire comparator_1_eq;
  wire [31:0] adder_1_out, and_out, multiplexer_1_out, multiplexer_2_out, multiplexer_3_out, shifter_1_out,
       XReg_q;

  // Probe on x
  assign and_out = XReg_q & 32'h3;  // AND_Gate and, 32 bits wide
  Multiplexer #(.width(32), .disabled(0), .enable("false")) multiplexer_1 (
    .in0(shifter_1_out), .in1(x), .out(multiplexer_1_out), .sel(start));
  Comparator #(.width(32)) comparator_1 (.a(and_out), .b(32'h1), .eq(comparator_1_eq));  // open: gt, lt
  Register #(.width(32), .trigger("falling")) XReg (.D(multiplexer_1_out), .Q(XReg_q), .clk(clk));  // open: en, clr
  Shifter #(.width(32), .shift("lr")) shifter_1 (.in(XReg_q), .\dist (5'b00001), .out(shifter_1_out));
  Adder #(.width(32)) adder_1 (.a(32'h1), .b(z), .out(adder_1_out));  // open: cin, cout
  // Probe on XReg_q
  Multiplexer #(.width(32), .disabled(0), .enable("false")) multiplexer_2 (
    .in0(z), .in1(adder_1_out), .out(multiplexer_2_out), .sel(comparator_1_eq));
  Multiplexer #(.width(32), .disabled(0), .enable("false")) multiplexer_3 (
    .in0(multiplexer_2_out), .in1({32{1'b0}}), .out(multiplexer_3_out), .sel(start));
  Comparator #(.width(32), .mode("unsigned")) comparator_2 (.a(XReg_q), .b({32{1'b0}}), .eq(rdy));  // open: gt, lt
  // Probe on z
  Register #(.width(32), .trigger("falling")) CReg (.D(multiplexer_3_out), .Q(z), .clk(clk));  // open: en, clr

  // Notes on the sheet:
  //   Registros
  //   Salidas
  //   z = Creg
  //   XReg = start ? x : (XReg>>1)
  //   rdy = XReg==0
  //   CReg = start ? 0 : ((XReg&3)==1 ? CReg+1 : CReg
  //   Si start es verdadero (1), entonces XReg toma el valor de x.
  //   Si start es verdadero (1), entonces CReg toma el valor de 0.
  //   Si start es falso (0), entonces CReg se actualiza de la siguiente manera:
  //   entonces CReg se incrementa en 1.
  //   De lo contrario, CReg permanece igual
  //   Si start es falso (0), entonces XReg se desplaza a la derecha una posición (XReg >> 1).
  //   Si los dos bits menos significativos de XReg (XReg & 3) son iguales a 1
  //   To debug your circuit
  //   with the hand, not from the left panel.
  //   select the module test-group from the left panel
  //   and then enter to the module GROUPS
  //   Advance the clock with control-T
  //   Restart the simulation with control-R
endmodule

module tester (
  input  rdy,
  input  [31:0] z,
  input  clk_in,
  output [31:0] x,
  output start,
  output success,
  output fail,
  output clk_out
);

  wire and_1_out, comparator_1_eq, d_ff_1_q;
  wire [4:0] counter_1_q;
  wire [23:0] rom_1_data;
  wire [31:0] bit_extender_1_out;

  Pull_Resistor #(.pull(1)) pull_resistor_1 (.node(rdy));
  Pull_Resistor pull_resistor_2 (.node(z));
  D_Flip_Flop #(.trigger("falling")) d_ff_1 (.clk(clk_in), .D(1'b1), .Q(d_ff_1_q));  // open: Qn, preset, en, reset
  and and_1 (and_1_out, d_ff_1_q, rdy, ~fail, ~rom_1_data[12]);  // AND_Gate
  Counter #(.width(5), .max('h1f), .trigger("falling")) counter_1 (
    .count(and_1_out), .Q(counter_1_q), .clk(clk_in));  // open: load, D, carry, clr
  ROM #(.addrWidth(5), .dataWidth(24)) rom_1 (
    .addr(counter_1_q), .data({rom_1_data[23:9], start, rom_1_data[7:0]}));  // open: sel
  assign bit_extender_1_out = {{26{1'b0}}, rom_1_data[21:16]};  // Bit_Extender bit_extender_1
  Comparator #(.width(32)) comparator_1 (.a(bit_extender_1_out), .b(z), .eq(comparator_1_eq));  // open: gt, lt
  ROM #(.addrWidth(3), .dataWidth(32)) rom_2 (.addr(rom_1_data[2:0]), .data(x));  // open: sel
  and and_2 (success, rom_1_data[12], rdy, comparator_1_eq);
  and and_3 (fail, rom_1_data[4], rdy, ~comparator_1_eq);  // AND_Gate
  and and_4 (clk_out, ~fail, clk_in);  // AND_Gate

  // Notes on the sheet:
  //   z[5:0] success[12] start[8]  valid[4] ex[1-0] 
  //   contents of rom_1 (hex, n*v repeats v):
  //   0 100 10 10 101 10011 102 30012 30012 103 40013 40013 40013 104 20014 20014 105 100015 100015 101015
  //   contents of rom_2 (hex, n*v repeats v):
  //   0 70 1a7 2e9 80000001 aaaaaaaa
endmodule
